// Digital circuit RV5-PROCESSOR.dig as structural Verilog
module RV5_PROCESSOR (
  input  clock
);

  wire a_eq_b, a_lt_b, branch_sel, carry, csr_opclear, csr_opset, csr_useimm, csr_wen, d_memwen, d_memwen_t,
       d_regwen, d_regwen_t, dm_mem_wen, dpc, dret_sel, ebreak_sel, ecall_sel, haltreq, IF_jal_sel,
       IF_jalr_sel, IF_mepc, IF_mret_sel, IF_mtvec, is_debug, is_progbuf, jump_progbuf, resumereq,
       rv5_control_logic_1_p8, rv5_control_logic_1_p9, rv5_control_logic_1_p10, rv5_control_logic_1_p11,
       rv5_control_logic_1_p13, rv5_control_logic_1_p14, rv5_control_logic_1_p15;
  wire [1:0] rv5_control_logic_1_p6, rv5_control_logic_1_p12;
  wire [2:0] funct3, rv5_control_logic_1_p4;
  wire [4:0] d_rd, d_rd_t, d_rs1, d_rs1_t;
  wire [6:0] inst;
  wire [11:0] funct12;
  wire [31:0] alu_out, and_1_out, csr_out, d_rdin, d_rdin_t, dcsr, dm_mem_addr, dm_mem_rdata, dm_mem_wdata,
       ID_pc, IF_imm_signext, multiplexer_1_out, multiplexer_2_out, multiplexer_3_out, multiplexer_4_out,
       multiplexer_5_out, not_1_out, or_1_out, ra, rv5_gpr_1_p8, rv5_memory_1_p13;
  wire [31:2] add_1_s;

  RV5_DEBUG_MODULE rv5_debug_module_1 (
    .clk(clock), .dcsr(dcsr), .dm_mem_rdata(dm_mem_rdata), .ra(ra), .is_debug(is_debug),
    .is_progbuf(is_progbuf), .d_regwen(d_regwen), .d_rdin(d_rdin), .d_memwen(d_memwen), .d_rd(d_rd),
    .d_rs1(d_rs1), .haltreq(haltreq), .resumereq(resumereq), .jump_progbuf(jump_progbuf),
    .dm_mem_wdata(dm_mem_wdata), .dm_mem_wen(dm_mem_wen), .dm_mem_addr(dm_mem_addr), .d_regwen_2(d_regwen_t),
    .d_rdin_2(d_rdin_t), .d_memwen_2(d_memwen_t), .d_rd_2(d_rd_t), .d_rs1_2(d_rs1_t));
  // RV5_PCU rv5_pcu_1: pin names not known; wires that end beside it: IF_imm_signext, alu_out, IF_mtvec, IF_mepc, dpc, branch_sel, IF_jal_sel, IF_jalr_sel, ecall_sel, IF_mret_sel, dcsr, dret_sel, haltreq, jump_progbuf, resumereq, ebreak_sel, funct3, a_eq_b, a_lt_b, carry, clock, ID_pc, is_debug, is_progbuf
  Multiplexer #(.Bits(32)) multiplexer_1 (
    .sel(csr_useimm), .in_0(ra), .in_1({{27{1'b0}}, d_rs1}), .out(multiplexer_1_out));
  assign not_1_out = ~multiplexer_1_out;  // Not not_1, 32 bits wide
  assign and_1_out = not_1_out & csr_out;  // And and_1, 32 bits wide
  assign or_1_out = multiplexer_1_out | csr_out;  // Or or_1, 32 bits wide
  // RV5_CONTROL_LOGIC rv5_control_logic_1: pin names not known; wires that end beside it: inst, funct3, funct12, rv5_control_logic_1_p4, d_regwen, rv5_control_logic_1_p6, d_memwen, rv5_control_logic_1_p8, rv5_control_logic_1_p9, rv5_control_logic_1_p10, rv5_control_logic_1_p11, rv5_control_logic_1_p12, rv5_control_logic_1_p13, rv5_control_logic_1_p14, rv5_control_logic_1_p15, branch_sel, IF_jal_sel, IF_jalr_sel, csr_wen, csr_opset, csr_opclear
  Multiplexer #(.Bits(32)) multiplexer_2 (
    .sel(csr_opclear), .in_0(multiplexer_1_out), .in_1(and_1_out), .out(multiplexer_2_out));
  Multiplexer #(.Bits(32)) multiplexer_3 (
    .sel(csr_opset), .in_0(multiplexer_2_out), .in_1(or_1_out), .out(multiplexer_3_out));
  RV5_IMM_GEN rv5_imm_gen_1 (
    .INSTR_32({funct12, d_rs1, funct3, d_rd, inst}), .imm_sel(rv5_control_logic_1_p4), .imm(IF_imm_signext));
  // RV5_CSR rv5_csr_1: pin names not known; wires that end beside it: csr_useimm, ecall_sel, ebreak_sel, IF_mret_sel, dret_sel, clock, funct12, multiplexer_3_out, csr_wen, ID_pc, ecall_sel, IF_mret_sel, ebreak_sel, is_debug, haltreq, csr_out, IF_mtvec, IF_mepc, dcsr, dpc
  // RV5_GPR rv5_gpr_1: pin names not known; wires that end beside it: d_rs1_t, funct12[4:0], d_rdin_t, clock, d_rd_t, d_regwen_t, ra, rv5_gpr_1_p8
  Multiplexer #(.Selector_Bits(2), .Bits(32)) multiplexer_4 (
    .sel(rv5_control_logic_1_p12), .in_0(ra), .in_1(ID_pc), .in_2({32{1'b0}}), .in_3({32{1'b0}}),
    .out(multiplexer_4_out));
  Multiplexer #(.Bits(32)) multiplexer_5 (
    .sel(rv5_control_logic_1_p14), .in_0(rv5_gpr_1_p8), .in_1(IF_imm_signext), .out(multiplexer_5_out));
  // RV5_ALU rv5_alu_1: pin names not known; wires that end beside it: multiplexer_4_out, rv5_control_logic_1_p13, multiplexer_5_out, rv5_control_logic_1_p15, alu_out, carry, a_eq_b, a_lt_b
  // RV5_MEMORY rv5_memory_1: pin names not known; wires that end beside it: alu_out, rv5_gpr_1_p8, d_memwen_t, rv5_control_logic_1_p8, clock, rv5_control_logic_1_p9, rv5_control_logic_1_p10, rv5_control_logic_1_p11, ID_pc, dm_mem_addr, dm_mem_wen, dm_mem_wdata, rv5_memory_1_p13, {funct12, d_rs1, funct3, d_rd, inst}, dm_mem_rdata
  Add #(.Bits(30)) add_1 (.a(ID_pc[31:2]), .b({30{1'b0}}), .c_i(1'b1), .s(add_1_s));  // open: c_o
  Multiplexer #(.Selector_Bits(2), .Bits(32)) multiplexer_6 (
    .sel(rv5_control_logic_1_p6), .in_0(alu_out), .in_1({add_1_s, 2'b00}), .in_2(rv5_memory_1_p13),
    .in_3(csr_out), .out(d_rdin));

  // Other names for the same wires on the sheet: IF_a_eq_b = a_eq_b; IF_a_lt_b = a_lt_b; IF_alu_out[31:0] = alu_out;
  //   IF_branch_sel = branch_sel; IF_carry = carry; clk = clock; IF_dcsr[31:0] = dcsr; IF_dpc = dpc;
  //   IF_dret_sel = dret_sel; IF_ebreak_sel = ebreak_sel; IF_ecall_sel = ecall_sel;
  //   imm_signext[31:0] = IF_imm_signext; inst[31:7] = {funct12, d_rs1, funct3, d_rd}; IF_funct3[2:0] = funct3;
  //   rs1[4:0] = d_rs1; rs2[4:0] = funct12[4:0]; jal_sel = IF_jal_sel; jalr_sel = IF_jalr_sel; mepc = IF_mepc;
  //   mret_sel = IF_mret_sel; mtvec = IF_mtvec; pc[31:0] = ID_pc; ID_wb[31:0] = d_rdin; wb[31:0] = d_rdin

  // Notes on the sheet:
  //   clock: Hz: 50000
  //   RISC-V CPU:
  //   IF: Instruction fetch
  //   In a harvard-style CPU, there would
  //   be actual instruction memory here.
  //   Instead, we have a tunnel to our
  //   memory block and a tunnel back.
  //   ID: Instruction decode/register file read
  //   debug module stuff - ignore
  //   (unless curious)
  //   EX: Execute/address calculation
  //   MEM: Memory access
  //   WB: Write back
endmodule
